// Logisim project ALU Final.circ as structural Verilog: 4 circuits, main circuit main
module main (
  input  [3:0] A,
  input  [3:0] B,
  input  [3:0] S3_S2_S1_S0,
  output Carry,
  output [3:0] Output
);

  wire and_1_out, and_2_out, not_1_out, not_2_out, not_3_out, or_1_out;
  wire [1:0] not_5_out;
  wire [3:0] arithmetic_1_output, logical_1_output, shift_1_output;

  not not_1 (not_1_out, S3_S2_S1_S0[3]);
  and and_1 (and_1_out, not_1_out, S3_S2_S1_S0[2]);
  not not_2 (not_2_out, S3_S2_S1_S0[3]);
  and and_2 (and_2_out, not_2_out, not_3_out);
  not not_3 (not_3_out, S3_S2_S1_S0[2]);
  Arithmetic arithmetic_1 (.A(A), .B(B), .S3_S2_S1_S0(S3_S2_S1_S0), .Output(arithmetic_1_output), .Carry(Carry));
  Logical logical_1 (.A(A), .B(B), .S3_S2_S1_S0(S3_S2_S1_S0), .Output(logical_1_output));
  Shift shift_1 (.Input(A), .S3_S2_S1_S0(S3_S2_S1_S0), .Output(shift_1_output));
  not not_4 (not_5_out[1], and_1_out);
  or or_1 (or_1_out, and_2_out, S3_S2_S1_S0[3]);
  not not_5 (not_5_out[0], or_1_out);
  Multiplexer #(.select(2), .width(4), .enable("false")) multiplexer_1 (
    .in0(arithmetic_1_output), .in1(logical_1_output), .in2(shift_1_output), .out(Output), .sel(not_5_out));  // open: in3
endmodule

// S
module Shift (
  input  [3:0] Input,
  input  [3:0] S3_S2_S1_S0,
  output [3:0] Output
);

  wire A2S1_prime_out, A3S1S0_prime_out, and_1_out, and_2_out, multiplexer_1_out, multiplexer_2_out,
       not_1_out, not_2_out, or_1_out, or_2_out;
  wire [3:0] multiplexer_3_out;

  not not_1 (not_1_out, S3_S2_S1_S0[1]);
  and A2S1_prime (A2S1_prime_out, Input[2], not_1_out);
  and A3S1S0_prime (A3S1S0_prime_out, Input[3], S3_S2_S1_S0[1], not_2_out);
  or or_1 (or_1_out, A2S1_prime_out, A3S1S0_prime_out);
  and and_1 (and_1_out, S3_S2_S1_S0[0], or_1_out);
  Multiplexer #(.enable("false")) multiplexer_1 (
    .in0(1'b0), .in1(Input[3]), .out(multiplexer_1_out), .sel(S3_S2_S1_S0[2]));
  Multiplexer #(.select(2), .enable("false")) multiplexer_2 (
    .in0(1'b0), .in1(Input[0]), .in2(multiplexer_3_out[2]), .out(multiplexer_2_out),
    .sel({S3_S2_S1_S0[1], S3_S2_S1_S0[2]}));  // open: in3
  not not_2 (not_2_out, S3_S2_S1_S0[2]);
  and and_2 (and_2_out, Input[2], S3_S2_S1_S0[0]);
  Multiplexer #(.enable("false")) multiplexer_3 (
    .in0(Input[1]), .in1(multiplexer_1_out), .out(multiplexer_3_out[0]), .sel(S3_S2_S1_S0[0]));
  Multiplexer #(.enable("false")) multiplexer_4 (
    .in0(Input[2]), .in1(Input[0]), .out(multiplexer_3_out[1]), .sel(S3_S2_S1_S0[0]));
  Multiplexer #(.enable("false")) multiplexer_5 (
    .in0(Input[3]), .in1(Input[1]), .out(multiplexer_3_out[2]), .sel(S3_S2_S1_S0[0]));
  or or_2 (or_2_out, and_1_out, and_2_out);
  Multiplexer #(.enable("false")) multiplexer_6 (
    .in0(multiplexer_2_out), .in1(or_2_out), .out(multiplexer_3_out[3]), .sel(S3_S2_S1_S0[0]));
  assign Output = multiplexer_3_out & {4{S3_S2_S1_S0[3]}};  // AND_Gate AND_3, 4 bits wide

  // Notes on the sheet:
  //   Logical, Circular and Arithmetic shift Unit
endmodule

// L
module Logical (
  input  [3:0] A,
  input  [3:0] B,
  input  [3:0] S3_S2_S1_S0,
  output [3:0] Output
);

  wire [3:0] AND_out, not_1_out, OR_out, XOR_out;

  assign AND_out = A & B;  // AND_Gate AND, 4 bits wide
  assign OR_out = A | B;  // OR_Gate OR, 4 bits wide
  Multiplexer #(.select(4), .width(4), .enable("false")) multiplexer_1 (
    .in4(AND_out), .in5(OR_out), .in6(XOR_out), .in7(not_1_out), .out(Output), .sel(S3_S2_S1_S0));  // open: in0, in1, in2, in3, in8, in9, in10, in11, in12, in13, in14, in15
  assign not_1_out = ~A;  // NOT_Gate not_1, 4 bits wide
  assign XOR_out = A ^ B;  // XOR_Gate XOR, 4 bits wide

  // Notes on the sheet:
  //   Logical Operations
endmodule

// A
module Arithmetic (
  input  [3:0] A,
  input  [3:0] B,
  input  [3:0] S3_S2_S1_S0,
  output [3:0] Output,
  output Carry
);

  wire XOR_out;
  wire [3:0] multiplexer_1_out, not_1_out, not_2_out;

  assign not_1_out = ~B;  // NOT_Gate not_1, 4 bits wide
  assign not_2_out = ~4'b0000;  // NOT_Gate not_2, 4 bits wide
  xor XOR (XOR_out, S3_S2_S1_S0[0], S3_S2_S1_S0[1]);
  Multiplexer #(.select(4), .width(4), .enable("false")) multiplexer_1 (
    .in0(B), .in1(not_1_out), .in2(4'b0000), .in3(not_2_out), .in4(4'b0000), .in5(4'b0000), .in6(4'b0000),
    .in7(4'b0000), .in8(4'b0000), .in9(4'b0000), .in10(4'b0000), .in11(4'b0000), .in12(4'b0000),
    .in13(4'b0000), .in14(4'b0000), .in15(4'b0000), .out(multiplexer_1_out), .sel(S3_S2_S1_S0));
  Adder #(.width(4)) adder_1 (.a(A), .b(multiplexer_1_out), .out(Output), .cin(XOR_out), .cout(Carry));

  // Notes on the sheet:
  //   Adder, Subtracter, Incrementer, Decrementer
endmodule
